# Fritzing sketch electronic_design (saved by Fritzing 0.9.2b)
breadboards: 1

parts:
  RF1 = nRF8001 Bluetooth LE Breakout
  ARDUINO1 = Arduino Micro
  FSR1 = Basic Force Sensing Resistor (FSR) [package=THT]
  FSR2 = Basic Force Sensing Resistor (FSR) [package=THT]
  FSR3 = Basic Force Sensing Resistor (FSR) [package=THT]
  FSR4 = Basic Force Sensing Resistor (FSR) [package=THT]
  FSR5 = Basic Force Sensing Resistor (FSR) [package=THT]
  FSR6 = Basic Force Sensing Resistor (FSR) [package=THT]
  R1 = Resistor [tolerance=±5% resistance=1k package="0402 [SMD]"]
  R2 = Resistor [tolerance=±5% resistance=1k package="0402 [SMD]"]
  R3 = Resistor [tolerance=±5% resistance=1k package="0402 [SMD]"]
  R4 = Resistor [tolerance=±5% resistance=1k package="0402 [SMD]"]
  R5 = Resistor [tolerance=±5% resistance=1k package="0402 [SMD]"]
  R6 = Resistor [tolerance=±5% resistance=1k package="0402 [SMD]"]
  R7 = Resistor [tolerance=±5% resistance=1k package="0402 [SMD]"]
  FSR0 = Basic Force Sensing Resistor (FSR) [package=THT]
  S3 = Pushbutton [package=THT]
  Composant8 = PowerBoost 1000 Basic
  U1 = LIPO-110mAh [package=lipo-110]

nets:
  N1: RF1.SCK, ARDUINO1.SCK
  N2: RF1.MISO, ARDUINO1.MOSI
  N3: RF1.MOSI, ARDUINO1.MISO
  N4: RF1.REQ, ARDUINO1.D10
  N5: RF1.RDY, ARDUINO1.D2
  N6: RF1.RST, ARDUINO1.D9
  GND: RF1.GND, ARDUINO1.GND#31, Composant8.GND, U1.-
  VIN: RF1.VIN, ARDUINO1.5V, FSR2.pin_0, FSR3.pin_0, FSR4.pin_0, FSR5.pin_0, FSR6.pin_0, FSR0.pin_0
  N7: ARDUINO1.GND#6, R1.Pin_1, R2.Pin_1, R3.Pin_1, R4.Pin_1, R5.Pin_1, R6.Pin_1, R7.Pin_1
  N8: ARDUINO1.D4, R3.Pin_0, FSR0.pin_1
  N9: ARDUINO1.A0, FSR1.pin_1, R2.Pin_0
  N10: ARDUINO1.A1, FSR6.pin_1, R5.Pin_0
  N11: ARDUINO1.A2, FSR2.pin_1, R4.Pin_0
  N12: ARDUINO1.A3, FSR3.pin_1, R6.Pin_0
  N13: ARDUINO1.A4, FSR5.pin_1, R7.Pin_0
  N14: ARDUINO1.A5, FSR4.pin_1, R1.Pin_0
  N15: ARDUINO1.VIN, S3.leg0
  N16: S3.leg1, Composant8.5.0V
  N17: Composant8.VBAT, U1.+

custom parts:
  nRF8001 Bluetooth LE Breakout: nRF8001 Breakout Board
  Arduino Micro: Arduino Micro Microcontroller
  PowerBoost 1000 Basic: The PowerBoost 1000 is a little DC/DC boost converter module that can run from 1.8V batteries or higher, and convert the battery output to 5.2V DC for running your 5V projects. At its heart is a TPS61030 boost converter from TI. This boost converter chip has some really nice extras such as low battery detection, 4A internal switch, synchronous conversion, excellent efficiency, and 700KHz high-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

// code stored in the sketch: lypoly.ino
<?xml version='1.0' encoding='UTF-8'?>
<module fritzingVersion='0.5.2b.02.18.4756' moduleId='PowerCell-v13'>
<version>4</version>
<date>2014-11-03</date>
<author>SFE and Fritzing</author>
<description>The PowerCell board is a single cell LiPo boost converter (to 3.3V and 5V) and micro-USB charger in one. The board comes with a JST connector for a single cell LiPo battery, a micro-USB connector for the 5V charge input, and selectable 3.3V and 5V output pins (labeled ?out?). There are also two charge pins broken out (labeled ?charge?), so you can use another 5V power source to charge the batteries, if you don?t have a micro-USB cable.
We?ve also broken out the power-save and enable pins, so that you can have full control of the switching regulator. Keep in mind, if you keep your battery connected to the Powercell, it is recommended that you disable the switching regulator (pull EN low) in order to prevent the battery from discharging and reaching the under voltage cutoff on the battery itself. There is also an under-voltage lockout on the Powercell board which is tied to a solder jumper so that you can disable it if you like.
The micro-USB charger uses the MCP73831 and allows you to charge 3.7V LiPo cells at a rate of 100mA max. If you want to charge at a faster rate, you will need to connect a separate power supply to the pins labeled ?5V? and ?GND? under the label ?charge?.
The boost converter is based on the TPS61200 from TI and has solder jumper selectable 5V and 3.3V output, and an under voltage protection of 2.6V (which can be disabled via solder jumper on the back of the PCB).
Note: This board does not have reverse polarity protection, so please be sure to recognize the polarity of your connections!

Dimensions: 1.03 x 0.95&quot;

Features:

- MCP73831 Single Cell LiPo charger at 500mA
- TPS61200 Boost Converter
- Selectable output voltage 3.3 or 5V
- 5V @ 600mA max
- 3.3V @ 200mA max
- Undervoltage lock out at 2.6V (with disable jumper)
- Quiescent current, less than 55uA
- JST connector for LiPo battery
- micro-USB connector for charge power source
- Inductor: 4.7uH, 1.2A Sumida CDRH2D18
- Over temperature protection
</description>
<title>Power Cell LiPo Charger/Booster</title>
<url>https://www.sparkfun.com/products/11231</url>
<tags>
<tag>SparkFun</tag>
</tags>
<properties>
<property name='family'>Power Cell LiPo Charger/Booster</property>
</properties>
<views>
<breadboardView>
<layers image='breadboard/PowerCell-v13.svg'>
<layer layerId='breadboard'/>
</layers>
</breadboardView>
<schematicView>
<layers image='schematic/PowerCell-v13.svg'>
<layer layerId='schematic'/>
</layers>
</schematicView>
<pcbView>
<layers image='pcb/PowerCell-v13.svg'>
<layer layerId='copper1'/>
<layer layerId='silkscreen'/>
<layer layerId='copper0'/>
</layers>
</pcbView>
<iconView>
<layers image='breadboard/PowerCell-v13.svg'>
<layer layerId='icon'/>
</layers>
</iconView>
</views>
<connectors>
<connector id='connector18' type='female' name='VCC'>
<description>VCC</description><views>
<breadboardView>
<p layer='breadboard' svgId='connector18pin'/></breadboardView>
<schematicView>
<p layer='schematic' svgId='connector18pin' terminalId='connector18terminal'/></schematicView>
<pcbView>
<p layer='copper0' svgId='connector18pad'/><p layer='copper1' svgId='connector18pad'/></pcbView>
</views>
</connector>
<connector id='connector19' type='female' name='GND'>
<description>GND</description><views>
<breadboardView>
<p layer='breadboard' svgId='connector19pin'/></breadboardView>
<schematicView>
<p layer='schematic' svgId='connector19pin' terminalId='connector19terminal'/></schematicView>
<pcbView>
<p layer='copper0' svgId='connector19pad'/><p layer='copper1' svgId='connector19pad'/></pcbView>
</views>
</connector>
<connector id='connector20' type='female' name='5VIN'>
<description>5VIN</description><views>
<breadboardView>
<p layer='breadboard' svgId='connector20pin'/></breadboardView>
<schematicView>
<p layer='schematic' svgId='connector20pin' terminalId='connector20terminal'/></schematicView>
<pcbView>
<p layer='copper0' svgId='connector20pad'/><p layer='copper1' svgId='connector20pad'/></pcbView>
</views>
</connector>
<connector id='connector21' type='female' name='GND'>
<description>GND</description><views>
<breadboardView>
<p layer='breadboard' svgId='connector21pin'/></breadboardView>
<schematicView>
<p layer='schematic' svgId='connector21pin' terminalId='connector21terminal'/></schematicView>
<pcbView>
<p layer='copper0' svgId='connector21pad'/><p layer='copper1' svgId='connector21pad'/></pcbView>
</views>
</connector>
<connector id='connector22' type='female' name='VBATT'>
<description>VBATT</description><views>
<breadboardView>
<p layer='breadboard' svgId='connector22pin'/></breadboardView>
<schematicView>
<p layer='schematic' svgId='connector22pin' terminalId='connector22terminal'/></schematicView>
<pcbView>
<p layer='copper0' svgId='connector22pad'/><p layer='copper1' svgId='connector22pad'/></pcbView>
</views>
</connector>
<connector id='connector23' type='female' name='GND'>
<description>GND</description><views>
<breadboardView>
<p layer='breadboard' svgId='connector23pin'/></breadboardView>
<schematicView>
<p layer='schematic' svgId='connector23pin' terminalId='connector23terminal'/></schematicView>
<pcbView>
<p layer='copper0' svgId='connector23pad'/><p layer='copper1' svgId='connector23pad'/></pcbView>
</views>
</connector>
<connector id='connector24' type='female' name='PS'>
<description>PS</description><views>
<breadboardView>
<p layer='breadboard' svgId='connector24pin'/></breadboardView>
<schematicView>
<p layer='schematic' svgId='connector24pin' terminalId='connector24terminal'/></schematicView>
<pcbView>
<p layer='copper0' svgId='connector24pad'/><p layer='copper1' svgId='connector24pad'/></pcbView>
</views>
</connector>
<connector id='connector25' type='female' name='EN'>
<description>EN</description><views>
<breadboardView>
<p layer='breadboard' svgId='connector25pin'/></breadboardView>
<schematicView>
<p layer='schematic' svgId='connector25pin' terminalId='connector25terminal'/></schematicView>
<pcbView>
<p layer='copper0' svgId='connector25pad'/><p layer='copper1' svgId='connector25pad'/></pcbView>
</views>
</connector>
</connectors>
<buses>
<bus id='gnd'>
<nodeMember connectorId='connector19'/>
<nodeMember connectorId='connector21'/>
<nodeMember connectorId='connector23'/>
</bus>
</buses>
</module>
